# Fritzing sketch RelayShield (saved by Fritzing 0.9.3b)
circuit board: 3.01107cm x 5.49174cm
breadboards: 1

parts:
  Part1 = Arduino Uno (Rev3)
  J1 = Screw terminal - 2 pins [package=THT]  # not connected
  J2 = Screw terminal - 2 pins [package=THT]  # not connected
  J3 = Screw terminal - 2 pins [package=THT]
  J4 = Screw terminal - 2 pins [package=THT]
  J5 = Screw terminal - 2 pins [package=THT]  # not connected
  J6 = Screw terminal - 2 pins [package=THT]  # not connected

nets:
  N1: Part1.5V, J3.pin1
  N2: Part1.GND, J3.pin2, J4.pin1
  N3: Part1.VIN, J4.pin2
