# Fritzing sketch mcopy_MONO_JK99_shield (saved by Fritzing 0.9.5d)
circuit board: 2.97497cm x 5.28509cm
breadboards: 1

parts:
  Part1 = Arduino Uno (Rev3)
  part = Screw terminal - 2 pins [package=THT]
  part_2 = Screw terminal - 2 pins [package=THT]
  part_3 = Screw terminal - 2 pins [package=THT]
  part_4 = Screw terminal - 2 pins [package=THT]
  FWD = Screw terminal - 2 pins [package=THT]
  BWD = Screw terminal - 2 pins [package=THT]

nets:
  N1: Part1.D8, FWD.pin1
  N2: Part1.D9_PWM, BWD.pin1
  N3: Part1.GND, part_2.pin2, part_4.pin1, part_4.pin2, FWD.pin2, BWD.pin2
  N4: Part1.D3_PWM, part.pin1
  N5: Part1.D4, part.pin2
  N6: Part1.D5_PWM, part_3.pin1
  N7: Part1.D6_PWM, part_3.pin2
  N8: Part1.5V, part_2.pin1

notes:
  proj adv [3]
  proj rew [4]
  takeup adv [5]
  takeup rew [6]
  [5V]
  [GND]
  mcopy JK100.1
